# Fritzing sketch schematic (saved by Fritzing 0.9.3b)
breadboards: 1

parts:
  Raspberry_Pi_1 = Raspberry Pi 3 [part_number=RPI-3-V1.2]
  R1 = Resistor [tolerance=±5% resistance=300 package=THT]
  R2 = Resistor [tolerance=±5% resistance=300 package=THT]
  R3 = Resistor [tolerance=±5% resistance=300 package=THT]
  ERR = LED - 5mm [color="Red (633nm)" package="5 mm [THT]"]
  LED2 = LED - 5mm [color="Green (555nm)" package="5 mm [THT]"]
  LED3 = LED - 5mm [color="Green (555nm)" package="5 mm [THT]"]
  STRT/STOP = Taiway 100-SP-X-T1 SPDT Miniature Toggle Switch [part_number=100-SP-X-T1-0-0-B1-M1 package=THT]
  Part1 = NRF24L01+ Breakout Board

nets:
  N1: Raspberry_Pi_1.GPIO22, Part1.IRQ
  N2: Raspberry_Pi_1.GPIO10, Part1.MOSI
  N3: Raspberry_Pi_1.GPIO9, Part1.MISO
  N4: Raspberry_Pi_1.GPIO11, Part1.SCK
  N5: Raspberry_Pi_1.GPIO5, R1.Pin_1
  N6: Raspberry_Pi_1.GPIO26, STRT/STOP.COM
  N7: Raspberry_Pi_1.GPIO8, Part1.CS
  N8: Raspberry_Pi_1.GPIO25, Part1.CE
  N9: Raspberry_Pi_1.GPIO24, R3.Pin_1
  N10: Raspberry_Pi_1.GPIO23, R2.Pin_1
  N11: R1.Pin_0, ERR.cathode
  N12: R2.Pin_0, LED3.cathode
  N13: R3.Pin_0, LED2.cathode
  3.3V: ERR.anode, LED2.anode, LED3.anode, Part1.VCC
  GND: STRT/STOP.L2, Part1.GND

notes:
  OpenHAB / MySensors RPi 1U enclosure, 1U converted Sokekris net6501 enclosure for Raspberry Pi-s with I/O additions, 1
